# Fritzing sketch 4thButterWorthLPF_100mH (saved by Fritzing 0.9.3b)
breadboards: 1

parts:
  L1 = Inductor [package="400 mil [THT]"]
  C1 = Film/Foil Capacitor [capacitance=100nF voltage=35V package="5mm [THT, pp]"]
  IC1 = Dual Op-Amp [package=dip08]
  L2 = Inductor [package="400 mil [THT]"]
  R1 = Resistor [tolerance=±5% resistance=270 package=THT]
  C2 = Film/Foil Capacitor [capacitance=100nF voltage=35V package="5mm [THT, pp]"]
  C3 = Ceramic Capacitor [capacitance=100nF package="100 mil [THT, multilayer]"]
  C4 = Ceramic Capacitor [capacitance=100nF package="100 mil [THT, multilayer]"]
  C5 = Electrolytic Capacitor [capacitance=1µF package="100 mil [THT, electrolytic]"]
  C6 = Electrolytic Capacitor [capacitance=1µF package="100 mil [THT, electrolytic]"]
  R2 = Resistor [tolerance=±5% resistance=1k package=THT]
  R3 = Resistor [tolerance=±5% resistance=10k package=THT]

nets:
  N1: L1.pin_0, C1.-, IC1.A_+IN
  N2: L1.pin_1, R2.Pin_0
  N3: C1.+, IC1.B_+IN, C2.+, C3.0, C4.1, C5.-, C6.+, R3.Pin_1
  N4: IC1.A_OUT, IC1.A_-IN, R1.Pin_1
  N5: IC1.A_V-, C4.0, C6.-
  N6: IC1.B_-IN, IC1.B_OUT
  N7: IC1.A_V+, C3.1, C5.+
  N8: L2.pin_0, C2.-, R3.Pin_0
  N9: L2.pin_1, R1.Pin_0

notes:
  IN
  OUT
  GND
  VCC
  VEE
  GND
