# Fritzing sketch 4thButterWorthLPF_100mH_NB (saved by Fritzing 0.9.3b)
breadboards: 1

parts:
  L1 = Inductor [package="400 mil [THT]"]
  C1 = Film/Foil Capacitor [capacitance=100nF voltage=35V package="5mm [THT, pp]"]
  L2 = Inductor [package="400 mil [THT]"]
  R1 = Resistor [tolerance=±5% resistance=270 package=THT]
  C2 = Film/Foil Capacitor [capacitance=100nF voltage=35V package="5mm [THT, pp]"]
  R2 = Resistor [tolerance=±5% resistance=1k package=THT]

nets:
  N1: L1.pin_0, C1.-, R1.Pin_1
  N2: L1.pin_1, R2.Pin_0
  N3: C1.+, C2.+
  N4: L2.pin_0, C2.-
  N5: L2.pin_1, R1.Pin_0

notes:
  IN
  OUT
  GND
  NC
