# Fritzing sketch 4thButterWorthLPF_VCVS (saved by Fritzing 0.9.3b)
breadboards: 1

parts:
  IC1 = Dual Op-Amp [package=dip08]
  C1 = Film/Foil Capacitor [capacitance=100nF voltage=35V package="5mm [THT, pp]"]
  R1 = Resistor [tolerance=±5% resistance=12k package=THT]
  C2 = Film/Foil Capacitor [capacitance=100nF voltage=35V package="5mm [THT, pp]"]
  R2 = Resistor [tolerance=±5% resistance=33k package=THT]
  R3 = Resistor [tolerance=±5% resistance=27k package=THT]
  C3 = Film/Foil Capacitor [capacitance=100nF voltage=35V package="5mm [THT, pp]"]
  C4 = Film/Foil Capacitor [capacitance=100nF voltage=35V package="5mm [THT, pp]"]
  R4 = Resistor [tolerance=±5% resistance=82k package=THT]
  C5 = Ceramic Capacitor [capacitance=100nF package="100 mil [THT, multilayer]"]
  C6 = Ceramic Capacitor [capacitance=100nF package="100 mil [THT, multilayer]"]
  C7 = Electrolytic Capacitor [capacitance=1µF package="100 mil [THT, electrolytic]"]
  C8 = Electrolytic Capacitor [capacitance=1µF package="100 mil [THT, electrolytic]"]

nets:
  N1: IC1.A_OUT, IC1.A_-IN, C2.-, R4.Pin_1
  N2: IC1.A_+IN, C1.-, R1.Pin_0
  N3: IC1.A_V-, C6.0, C8.+
  N4: IC1.B_+IN, R3.Pin_0, C3.+
  N5: IC1.B_-IN, IC1.B_OUT, C4.+
  N6: IC1.A_V+, C5.1, C7.+
  N7: C1.+, C3.-, C5.0, C6.1, C7.-, C8.-
  N8: R1.Pin_1, C2.+, R2.Pin_0
  N9: R3.Pin_1, C4.-, R4.Pin_0

notes:
  GND
  VCC
  VEE
  GND
  IN
  OUT
