# Fritzing sketch fritzing_4thButterWorthLPF_MFB_Fail (saved by Fritzing 0.9.3b)
breadboards: 1

parts:
  IC1 = Dual Op-Amp [package=dip08]
  C1 = Film/Foil Capacitor [capacitance=100nF voltage=35V package="5mm [THT, pp]"]
  R1 = Resistor [tolerance=±5% resistance=12k package=THT]
  C2 = Film/Foil Capacitor [capacitance=100nF voltage=35V package="5mm [THT, pp]"]
  R2 = Resistor [tolerance=±5% resistance=4.7k package=THT]
  R3 = Resistor [tolerance=±5% resistance=4.7k package=THT]
  R4 = Resistor [tolerance=±5% resistance=12k package=THT]
  C3 = Film/Foil Capacitor [capacitance=100nF voltage=35V package="5mm [THT, pp]"]
  R5 = Resistor [tolerance=±5% resistance=3.3k package=THT]
  C4 = Film/Foil Capacitor [capacitance=100nF voltage=35V package="5mm [THT, pp]"]
  R6 = Resistor [tolerance=±5% resistance=3.3k package=THT]
  C5 = Ceramic Capacitor [capacitance=100nF package="100 mil [THT, multilayer]"]
  C6 = Ceramic Capacitor [capacitance=100nF package="100 mil [THT, multilayer]"]
  C7 = Electrolytic Capacitor [capacitance=1µF package="100 mil [THT, electrolytic]"]
  C8 = Electrolytic Capacitor [capacitance=1µF package="100 mil [THT, electrolytic]"]
  C9 = Film/Foil Capacitor [capacitance=100nF voltage=35V package="5mm [THT, pp]"]

nets:
  N1: IC1.A_OUT, C1.-, R3.Pin_0, R5.Pin_1
  N2: IC1.A_-IN, C1.+, R1.Pin_0, R3.Pin_1
  N3: IC1.A_+IN, IC1.B_+IN, C2.+, C4.-, C5.0, C6.0, C7.-, C8.+, C9.-
  N4: IC1.A_V-, C5.1, C8.-
  N5: IC1.B_-IN, R4.Pin_0, C3.+
  N6: IC1.B_OUT, C3.-, R6.Pin_0
  N7: IC1.A_V+, C6.1, C7.+
  N8: R1.Pin_1, C2.-, R2.Pin_0
  N9: R4.Pin_1, R5.Pin_0, C4.+, R6.Pin_1, C9.+

notes:
  IN
  OUT
  GND
  VCC
  VEE
  GND
